// Logisim project logisim_basys3.circ as structural Verilog: 4 circuits, main circuit main
module main (
  input  g,
  input  f,
  input  a,
  input  b,
  input  AN0,
  input  AN1,
  input  AN2,
  input  AN3,
  input  e,
  input  d,
  input  c,
  input  dp,
  input  sw15,
  input  sw14,
  input  sw13,
  input  sw12,
  input  sw11,
  input  sw10,
  input  sw9,
  input  sw8,
  input  sw7,
  input  sw6,
  input  sw5,
  input  sw4,
  input  sw3,
  input  sw2,
  input  sw1,
  input  sw0
);

  wire n7_led_1_a0, n7_led_1_a1, n7_led_1_a2, n7_led_1_a3, n7_led_1_b0, n7_led_1_b1, n7_led_1_b2,
       n7_led_1_b3, n7_led_1_c0, n7_led_1_c1, n7_led_1_c2, n7_led_1_c3, n7_led_1_d0, n7_led_1_d1,
       n7_led_1_d2, n7_led_1_d3, n7_led_1_dp0, n7_led_1_dp1, n7_led_1_dp1_2, n7_led_1_dp2, n7_led_1_e0,
       n7_led_1_e1, n7_led_1_e2, n7_led_1_e3, n7_led_1_f0, n7_led_1_f1, n7_led_1_f2, n7_led_1_f3,
       n7_led_1_g0, n7_led_1_g1, n7_led_1_g2, n7_led_1_g3;

  Button BTNC ();  // open: out
  LED LD0 ();  // open: in
  Button BTND ();  // open: out
  LED LD1 ();  // open: in
  Button BTNLU ();  // open: out
  Button BTNR ();  // open: out
  LED LD3 ();  // open: in
  LED LD2 ();  // open: in
  Button BTNL ();  // open: out
  LED LD5 ();  // open: in
  LED LD4 ();  // open: in
  _7_led u_7_led_1 (
    .g(g), .f(f), .a(a), .b(b), .AN0(AN0), .AN1(AN1), .AN2(AN2), .AN3(AN3), .e(e), .d(d), .c(c), .dp(dp),
    .g0(n7_led_1_g0), .g1(n7_led_1_g1), .g2(n7_led_1_g2), .g3(n7_led_1_g3), .f0(n7_led_1_f0),
    .f1(n7_led_1_f1), .f2(n7_led_1_f2), .f3(n7_led_1_f3), .a0(n7_led_1_a0), .a1(n7_led_1_a1),
    .a2(n7_led_1_a2), .a3(n7_led_1_a3), .b0(n7_led_1_b0), .b1(n7_led_1_b1), .b2(n7_led_1_b2),
    .b3(n7_led_1_b3), .e0(n7_led_1_e0), .e1(n7_led_1_e1), .e2(n7_led_1_e2), .e3(n7_led_1_e3),
    .d0(n7_led_1_d0), .d1(n7_led_1_d1), .d2(n7_led_1_d2), .d3(n7_led_1_d3), .c0(n7_led_1_c0),
    .c1(n7_led_1_c1), .c2(n7_led_1_c2), .c3(n7_led_1_c3), .dp0(n7_led_1_dp0), .dp1(n7_led_1_dp1),
    .dp2(n7_led_1_dp2), .dp1_2(n7_led_1_dp1_2));
  LED LD6 ();  // open: in
  LED LD8 ();  // open: in
  LED LD7 ();  // open: in
  LED LD9 ();  // open: in
  LED LD11 ();  // open: in
  LED LD10 ();  // open: in
  _7_Segment_Display u_7_segment_display_1 (
    .g(n7_led_1_g3), .f(n7_led_1_f3), .a(n7_led_1_a3), .b(n7_led_1_b3), .e(n7_led_1_e3), .d(n7_led_1_d3),
    .c(n7_led_1_c3), .dp(n7_led_1_dp1_2));
  LED LD12 ();  // open: in
  LED LD13 ();  // open: in
  _7_Segment_Display u_7_segment_display_2 (
    .g(n7_led_1_g2), .f(n7_led_1_f2), .a(n7_led_1_a2), .b(n7_led_1_b2), .e(n7_led_1_e2), .d(n7_led_1_d2),
    .c(n7_led_1_c2), .dp(n7_led_1_dp2));
  _7_Segment_Display u_7_segment_display_3 (
    .g(n7_led_1_g1), .f(n7_led_1_f1), .a(n7_led_1_a1), .b(n7_led_1_b1), .e(n7_led_1_e1), .d(n7_led_1_d1),
    .c(n7_led_1_c1), .dp(n7_led_1_dp1));
  LED LD14 ();  // open: in
  _7_Segment_Display u_7_segment_display_4 (
    .g(n7_led_1_g0), .f(n7_led_1_f0), .a(n7_led_1_a0), .b(n7_led_1_b0), .e(n7_led_1_e0), .d(n7_led_1_d0),
    .c(n7_led_1_c0), .dp(n7_led_1_dp0));
  LED LD15 ();  // open: in
endmodule

module _7_led (
  input  g,
  input  f,
  input  a,
  input  b,
  input  AN0,
  input  AN1,
  input  AN2,
  input  AN3,
  input  e,
  input  d,
  input  c,
  input  dp,
  output g0,
  output g1,
  output g2,
  output g3,
  output f0,
  output f1,
  output f2,
  output f3,
  output a0,
  output a1,
  output a2,
  output a3,
  output b0,
  output b1,
  output b2,
  output b3,
  output e0,
  output e1,
  output e2,
  output e3,
  output d0,
  output d1,
  output d2,
  output d3,
  output c0,
  output c1,
  output c2,
  output c3,
  output dp0,
  output dp1,
  output dp2,
  output dp1_2
);

  and and_1 (g0, g, AN0);
  and and_2 (f0, f, AN0);
  and and_3 (a0, a, AN0);
  and and_4 (b0, b, AN0);
  and and_5 (e0, e, AN0);
  and and_6 (d0, d, AN0);
  and and_7 (c0, c, AN0);
  and and_8 (dp0, dp, AN0);
  and and_9 (g1, g, AN1);
  and and_10 (f1, f, AN1);
  and and_11 (a1, a, AN1);
  and and_12 (b1, b, AN1);
  and and_13 (e1, e, AN1);
  and and_14 (d1, d, AN1);
  and and_15 (c1, c, AN1);
  and and_16 (dp1, dp, AN1);
  and and_17 (g2, g, AN2);
  and and_18 (f2, f, AN2);
  and and_19 (a2, a, AN2);
  and and_20 (b2, b, AN2);
  and and_21 (e2, e, AN2);
  and and_22 (d2, d, AN2);
  and and_23 (c2, c, AN2);
  and and_24 (dp2, dp, AN2);
  and and_25 (g3, g, AN3);
  and and_26 (f3, f, AN3);
  and and_27 (a3, a, AN3);
  and and_28 (b3, b, AN3);
  and and_29 (e3, e, AN3);
  and and_30 (d3, d, AN3);
  and and_31 (c3, c, AN3);
  and and_32 (dp1_2, dp, AN3);
endmodule

module M2 (
  input  g,
  input  f,
  input  a,
  input  b,
  input  AN0,
  input  AN1,
  input  AN2,
  input  AN3,
  input  e,
  input  d,
  input  c,
  input  dp,
  input  sw15,
  input  sw14,
  input  sw13,
  input  sw12,
  input  sw11,
  input  sw10,
  input  sw9,
  input  sw8,
  input  sw7,
  input  sw6,
  input  sw5,
  input  sw4,
  input  sw3,
  input  sw2,
  input  sw1,
  input  sw0
);

  wire n7_led2_1_a0, n7_led2_1_a1, n7_led2_1_a2, n7_led2_1_a3, n7_led2_1_b0, n7_led2_1_b1, n7_led2_1_b2,
       n7_led2_1_b3, n7_led2_1_c0, n7_led2_1_c1, n7_led2_1_c2, n7_led2_1_c3, n7_led2_1_d0, n7_led2_1_d1,
       n7_led2_1_d2, n7_led2_1_d3, n7_led2_1_dp0, n7_led2_1_dp1, n7_led2_1_dp1_2, n7_led2_1_dp2,
       n7_led2_1_e0, n7_led2_1_e1, n7_led2_1_e2, n7_led2_1_e3, n7_led2_1_f0, n7_led2_1_f1, n7_led2_1_f2,
       n7_led2_1_f3, n7_led2_1_g0, n7_led2_1_g1, n7_led2_1_g2, n7_led2_1_g3;

  Button BTNC ();  // open: out
  LED LD0 ();  // open: in
  Button BTND ();  // open: out
  LED LD1 ();  // open: in
  Button BTNLU ();  // open: out
  Button BTNR ();  // open: out
  LED LD2 ();  // open: in
  LED LD3 ();  // open: in
  Button BTNL ();  // open: out
  LED LD5 ();  // open: in
  LED LD4 ();  // open: in
  _7_Led2 u_7_led2_1 (
    .g(g), .f(f), .a(a), .b(b), .AN0(AN0), .AN1(AN1), .AN2(AN2), .AN3(AN3), .e(e), .d(d), .c(c), .dp(dp),
    .g0(n7_led2_1_g0), .g1(n7_led2_1_g1), .g2(n7_led2_1_g2), .g3(n7_led2_1_g3), .f0(n7_led2_1_f0),
    .f1(n7_led2_1_f1), .f2(n7_led2_1_f2), .f3(n7_led2_1_f3), .a0(n7_led2_1_a0), .a1(n7_led2_1_a1),
    .a2(n7_led2_1_a2), .a3(n7_led2_1_a3), .b0(n7_led2_1_b0), .b1(n7_led2_1_b1), .b2(n7_led2_1_b2),
    .b3(n7_led2_1_b3), .e0(n7_led2_1_e0), .e1(n7_led2_1_e1), .e2(n7_led2_1_e2), .e3(n7_led2_1_e3),
    .d0(n7_led2_1_d0), .d1(n7_led2_1_d1), .d2(n7_led2_1_d2), .d3(n7_led2_1_d3), .c0(n7_led2_1_c0),
    .c1(n7_led2_1_c1), .c2(n7_led2_1_c2), .c3(n7_led2_1_c3), .dp0(n7_led2_1_dp0), .dp1(n7_led2_1_dp1),
    .dp2(n7_led2_1_dp2), .dp1_2(n7_led2_1_dp1_2));
  LED LD6 ();  // open: in
  LED LD7 ();  // open: in
  LED LD8 ();  // open: in
  LED LD9 ();  // open: in
  LED LD10 ();  // open: in
  LED LD11 ();  // open: in
  _7_Segment_Display u_7_segment_display_1 (
    .g(n7_led2_1_g3), .f(n7_led2_1_f3), .a(n7_led2_1_a3), .b(n7_led2_1_b3), .e(n7_led2_1_e3),
    .d(n7_led2_1_d3), .c(n7_led2_1_c3), .dp(n7_led2_1_dp1_2));
  LED LD12 ();  // open: in
  LED LD13 ();  // open: in
  _7_Segment_Display u_7_segment_display_2 (
    .g(n7_led2_1_g1), .f(n7_led2_1_f1), .a(n7_led2_1_a1), .b(n7_led2_1_b1), .e(n7_led2_1_e1),
    .d(n7_led2_1_d1), .c(n7_led2_1_c1), .dp(n7_led2_1_dp1));
  _7_Segment_Display u_7_segment_display_3 (
    .g(n7_led2_1_g2), .f(n7_led2_1_f2), .a(n7_led2_1_a2), .b(n7_led2_1_b2), .e(n7_led2_1_e2),
    .d(n7_led2_1_d2), .c(n7_led2_1_c2), .dp(n7_led2_1_dp2));
  LED LD14 ();  // open: in
  _7_Segment_Display u_7_segment_display_4 (
    .g(n7_led2_1_g0), .f(n7_led2_1_f0), .a(n7_led2_1_a0), .b(n7_led2_1_b0), .e(n7_led2_1_e0),
    .d(n7_led2_1_d0), .c(n7_led2_1_c0), .dp(n7_led2_1_dp0));
  LED LD15 ();  // open: in
endmodule

module _7_Led2 (
  input  g,
  input  f,
  input  a,
  input  b,
  input  AN0,
  input  AN1,
  input  AN2,
  input  AN3,
  input  e,
  input  d,
  input  c,
  input  dp,
  output g0,
  output g1,
  output g2,
  output g3,
  output f0,
  output f1,
  output f2,
  output f3,
  output a0,
  output a1,
  output a2,
  output a3,
  output b0,
  output b1,
  output b2,
  output b3,
  output e0,
  output e1,
  output e2,
  output e3,
  output d0,
  output d1,
  output d2,
  output d3,
  output c0,
  output c1,
  output c2,
  output c3,
  output dp0,
  output dp1,
  output dp2,
  output dp1_2
);

  wire not_1_out, not_2_out, not_3_out, not_4_out, not_5_out, not_6_out, not_7_out, not_8_out, not_9_out,
       not_10_out, not_11_out, not_12_out;

  not not_1 (not_1_out, AN0);
  not not_2 (not_2_out, g);
  not not_3 (not_3_out, f);
  not not_4 (not_4_out, a);
  not not_5 (not_5_out, b);
  not not_6 (not_6_out, e);
  not not_7 (not_7_out, d);
  not not_8 (not_8_out, c);
  not not_9 (not_9_out, dp);
  and and_1 (g0, not_2_out, not_1_out);
  and and_2 (f0, not_3_out, not_1_out);
  and and_3 (a0, not_4_out, not_1_out);
  and and_4 (b0, not_5_out, not_1_out);
  and and_5 (e0, not_6_out, not_1_out);
  and and_6 (d0, not_7_out, not_1_out);
  and and_7 (c0, not_8_out, not_1_out);
  and and_8 (dp0, not_9_out, not_1_out);
  not not_10 (not_10_out, AN1);
  and and_9 (g1, not_2_out, not_10_out);
  and and_10 (f1, not_3_out, not_10_out);
  and and_11 (a1, not_4_out, not_10_out);
  and and_12 (b1, not_5_out, not_10_out);
  and and_13 (e1, not_6_out, not_10_out);
  and and_14 (d1, not_7_out, not_10_out);
  and and_15 (c1, not_8_out, not_10_out);
  and and_16 (dp1, not_9_out, not_10_out);
  not not_11 (not_11_out, AN2);
  and and_17 (g2, not_2_out, not_11_out);
  and and_18 (f2, not_3_out, not_11_out);
  and and_19 (a2, not_4_out, not_11_out);
  and and_20 (b2, not_5_out, not_11_out);
  and and_21 (e2, not_6_out, not_11_out);
  and and_22 (d2, not_7_out, not_11_out);
  and and_23 (c2, not_8_out, not_11_out);
  and and_24 (dp2, not_9_out, not_11_out);
  not not_12 (not_12_out, AN3);
  and and_25 (g3, not_2_out, not_12_out);
  and and_26 (f3, not_3_out, not_12_out);
  and and_27 (a3, not_4_out, not_12_out);
  and and_28 (b3, not_5_out, not_12_out);
  and and_29 (e3, not_6_out, not_12_out);
  and and_30 (d3, not_7_out, not_12_out);
  and and_31 (c3, not_8_out, not_12_out);
  and and_32 (dp1_2, not_9_out, not_12_out);
endmodule
